# Fritzing sketch TM_BluetoothControl (saved by Fritzing 0.8.3b)

parts:
  Part1 = Bluetooth HC-05 Macho
  元件2 = Arduino Uno (Rev3)  # not connected
  元件3 = SRF05 Ultrasonic Rangefinder
  元件4 = Arduino Sensor Shield v5.0
  S1 = H-Bridge with L298N
  SERVO1 = Tower Pro SG90 servo [part_number=101246]
  U1 = ESP8266 WiFi Module [part_number=ESP8266]  # not connected
  M1 = DC Motor
  M2 = DC Motor
  元件5 = Arduino Mega 2560 (Rev3)  # not connected
  VCC1 = Battery

nets:
  N1: Part1.TXD, 元件4.D0(RX)
  N2: Part1.RXD, 元件4.D1(TX)
  N3: Part1.VCC, 元件4.+5V#126
  N4: Part1.GND, 元件4.GND#131
  N5: 元件3.VCC, 元件4.+5V#91
  N6: 元件3.Trig, 元件4.D3
  N7: 元件3.Echo, 元件4.D2
  N8: 元件3.GND, 元件4.GND#128
  N9: 元件4.D9, SERVO1.Signal
  N10: 元件4.D10, S1.IN3
  N11: 元件4.D11, S1.IN4
  N12: 元件4.GND#72, 元件4.GND#122, SERVO1.GND
  N13: 元件4.D5, S1.IN1
  N14: 元件4.D6, S1.IN2
  N15: 元件4.+5V#94, 元件4.+5V#107, SERVO1.+5V
  N16: S1.12V, VCC1.+
  N17: S1.M1-01, M1.pin_1
  N18: S1.M1-02, M1.pin_2
  N19: S1.M2-01, M2.pin_2
  N20: S1.M2-02, M2.pin_1

custom parts:
  H-Bridge with L298N: h-bridge
  Tower Pro SG90 servo: Original file by John De Cristofaro http://www.adafruit.com/products/1449 Adafruit Feedback Servo (Small) Edited by: e-radionica.com 28/9/2015
  ESP8266 WiFi Module: Generic WiFi Module based on the ESP8266 with onboard PCB antenna and UART communications
  Battery: Your standard 2x 18650 battery pack (7,4 Volts)
